# Fritzing sketch DS2438 Sondenadapter (saved by Fritzing 1.0.1rc)
stripboards: 1

parts:
  VR2 = DS2438 [part_number=DS2438 package=SO]
  J3 = screw terminal, 3 pins
  J4 = Screw terminal - 2 pins [package=THT]

nets (from the schematic view):
  N1: VR2.pin_1, J3.pin2, J4.pin2
  N2: VR2.pin_4, J4.pin1
  N3: VR2.pin_5, J3.pin3
  N4: VR2.pin_8, J3.pin1

custom parts:
  DS2438: 1-Wire DS2438 Smart Battery Monitor
